# Fritzing sketch rheadoor (saved by Fritzing 0.9.4)

parts:
  MCU1 = Raspberry Pi Zero
  Part2 = EasyDriver_v44
  Part3 = I2C level shifter bidirectional
  Part4 = Arduino Nano Every
  LED1 = LED - 5mm [color="Red (633nm)" package="5 mm [THT]"]
  R1 = Resistor [tolerance=±5% resistance=220 package=THT]

nets:
  N1: MCU1.pin_1, Part3.LV
  N2: MCU1.pin_3, Part3.LV2
  N3: MCU1.pin_5, Part3.LV1
  GND: MCU1.pin_6, MCU1.pin_25, MCU1.pin_34, Part2.GND, Part3.GND, Part3.HV3, Part4.RESET, Part4.GND, Part4.VIN, Part4.A6, Part4.A7, Part4.D13~, R1.Pin_1
  N4: MCU1.pin_7, Part3.LV3
  N5: MCU1.pin_8, LED1.anode
  N6: Part2.STEP, Part4.D2
  N7: Part2.DIR, Part4.D3~
  N8: Part2.MS1, Part4.D4
  N9: Part2.ENABLE, Part4.D6~
  N10: Part2.MS2, Part4.D5~
  N11: Part3.HV1, Part4.A5
  N12: Part3.HV2, Part4.A4
  N13: Part3.HV, Part4.D11/MOSI, Part4.+5V

notes:
  Green signal wire used by Arduino to tell Pi work is done
  Brown (SDA) and Blue (SCL) wires used for IC2 comms for Pi to tell Arduino to perform work
  Yellow (V) and Red (GND) wires used to power logic converter with 3.3v (L) for Pi and 5v (H) for Arduino
  #define stepPin 2 - Red wire
  #define dirPin 3 - Brown wire
  #define MS1 5 - Orange wire
  #define MS2 6 - Grey wire
  #define enablePin 7 - Green wire
  #define signalPin 20 - Green wire

custom parts:
  Arduino Nano Every: The Nano Every is Arduino’s 5V compatible board in the smallest available form factor: 45x18mm! The Arduino Nano is the preferred board for many projects requiring a small and easy to use microcontroller board. The small footprint and low price, make the Nano Every particularly suited for wearable inventions, low cost robotics, electronic musical instruments, and general use to control smaller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
